// Logisim project partial-store.circ as structural Verilog: 1 circuit, main circuit partial_store
module partial_store (
  input  [31:0] Instruction,
  input  [31:0] MemAddress,
  input  [31:0] DataFromReg,
  input  MemWEn,
  output [3:0] MemWriteMask,
  output [31:0] DataToMem
);

  wire comparator_4_eq, comparator_5_eq, comparator_6_eq, comparator_7_eq, comparator_8_eq, comparator_9_eq,
       is_sb, is_sh, is_sw, sb0, sb1, sb2, sb3, sh0, sh1;
  wire [3:0] mask_sel;
  wire [31:0] bit_extender_1_out, bit_extender_2_out, bit_extender_3_out, bit_extender_4_out,
       bit_extender_5_out, bit_extender_6_out, shifter_1_out, shifter_2_out, shifter_3_out, shifter_4_out;

  Priority_Encoder #(.select_enc(4)) priority_encoder_1 (
    .in1(sb0), .in2(sb1), .in3(sh0), .in4(sb2), .in8(sb3), .in12(sh1), .in15(is_sw), .out(mask_sel));  // open: in0, in5, in6, in7, in9, in10, in11, in13, in14, gs, en_out, en_in
  Comparator #(.width(3)) comparator_1 (.a(Instruction[14:12]), .b(3'b000), .eq(is_sb));  // open: gt, lt
  Comparator #(.width(3)) comparator_2 (.a(Instruction[14:12]), .b(3'b001), .eq(is_sh));  // open: gt, lt
  Comparator #(.width(3)) comparator_3 (.a(Instruction[14:12]), .b(3'b010), .eq(is_sw));  // open: gt, lt
  assign bit_extender_1_out = {{24{1'b0}}, DataFromReg[7:0]};  // Bit_Extender bit_extender_1
  assign bit_extender_2_out = {{24{1'b0}}, DataFromReg[7:0]};  // Bit_Extender bit_extender_2
  assign bit_extender_3_out = {{24{1'b0}}, DataFromReg[7:0]};  // Bit_Extender bit_extender_3
  assign bit_extender_4_out = {{24{1'b0}}, DataFromReg[7:0]};  // Bit_Extender bit_extender_4
  assign bit_extender_5_out = {{16{1'b0}}, DataFromReg[15:0]};  // Bit_Extender bit_extender_5
  assign bit_extender_6_out = {{16{1'b0}}, DataFromReg[15:0]};  // Bit_Extender bit_extender_6
  Comparator #(.width(2)) comparator_4 (.a(MemAddress[1:0]), .b(2'b00), .eq(comparator_4_eq));  // open: gt, lt
  Comparator #(.width(2)) comparator_5 (.a(MemAddress[1:0]), .b(2'b01), .eq(comparator_5_eq));  // open: gt, lt
  Comparator #(.width(2)) comparator_6 (.a(MemAddress[1:0]), .b(2'b10), .eq(comparator_6_eq));  // open: gt, lt
  Comparator #(.width(2)) comparator_7 (.a(MemAddress[1:0]), .b(2'b11), .eq(comparator_7_eq));  // open: gt, lt
  Shifter #(.width(32)) shifter_1 (.in(bit_extender_2_out), .\dist (5'b01000), .out(shifter_1_out));
  Shifter #(.width(32)) shifter_2 (.in(bit_extender_3_out), .\dist (5'b10000), .out(shifter_2_out));
  Shifter #(.width(32)) shifter_3 (.in(bit_extender_4_out), .\dist (5'b11000), .out(shifter_3_out));
  Shifter #(.width(32)) shifter_4 (.in(bit_extender_6_out), .\dist (5'b10000), .out(shifter_4_out));
  and and_1 (sb0, comparator_4_eq, is_sb);
  and and_2 (sb1, comparator_5_eq, is_sb);
  and and_3 (sb2, comparator_6_eq, is_sb);
  and and_4 (sb3, comparator_7_eq, is_sb);
  Multiplexer #(.select(4), .width(32)) multiplexer_1 (
    .in1(bit_extender_1_out), .in2(shifter_1_out), .in3(bit_extender_5_out), .in4(shifter_2_out),
    .in8(shifter_3_out), .in12(shifter_4_out), .in15(DataFromReg), .out(DataToMem), .sel(mask_sel));  // open: in0, in5, in6, in7, in9, in10, in11, in13, in14
  Comparator #(.width(2)) comparator_8 (.a(MemAddress[1:0]), .b(2'b00), .eq(comparator_8_eq));  // open: gt, lt
  Comparator #(.width(2)) comparator_9 (.a(MemAddress[1:0]), .b(2'b10), .eq(comparator_9_eq));  // open: gt, lt
  and and_5 (sh0, comparator_8_eq, is_sh);
  and and_6 (sh1, comparator_9_eq, is_sh);
  Multiplexer #(.width(4)) multiplexer_2 (.in0(4'b0000), .in1(mask_sel), .out(MemWriteMask), .sel(MemWEn));

  // Other names for the same wires on the sheet: func3[2:0] = Instruction[14:12];
  //   buttom_2_bits[1:0] = MemAddress[1:0]

  // Notes on the sheet:
  //   INPUTS to your circuit
  //   DON'T CHANGE THE LOCATIONS OF THE INPUTS AND OUTPUTS!
  //   OUTPUT from your circuit
endmodule
